// Logisim project Corrado-29407A.circ as structural Verilog: 7 circuits, main circuit Ese1
module Ese1 (
  input  C,
  input  A,
  input  T,
  input  F,
  output out_5,
  output out_6,
  output out_7
);

  wire and_1_out, and_2_out, and_3_out, and_4_out, and_5_out, and_6_out, and_7_out, and_8_out, and_9_out,
       and_10_out, and_11_out, and_12_out, and_13_out, and_14_out, and_15_out, and_16_out, and_17_out;

  and and_1 (and_1_out, ~C, ~A, T, F);  // AND_Gate
  and and_2 (and_2_out, ~C, A, ~T, F);  // AND_Gate
  and and_3 (and_3_out, ~C, A, T, ~F);  // AND_Gate
  and and_4 (and_4_out, ~C, A, T, F);  // AND_Gate
  and and_5 (and_5_out, C, ~A, ~T, F);  // AND_Gate
  and and_6 (and_6_out, C, ~A, T, ~F);  // AND_Gate
  and and_7 (and_7_out, C, ~A, T, F);  // AND_Gate
  and and_8 (and_8_out, C, A, ~T, ~F);  // AND_Gate
  and and_9 (and_9_out, C, A, ~T, F);  // AND_Gate
  and and_10 (and_10_out, C, A, T, ~F);  // AND_Gate
  and and_11 (and_11_out, C, A, T, F);
  and and_12 (and_12_out, A, F);
  and and_13 (and_13_out, A, T);
  and and_14 (and_14_out, C, F);
  and and_15 (and_15_out, T, C);
  and and_16 (and_16_out, T, F);
  and and_17 (and_17_out, A, C);
  or or_1 (out_5, and_1_out, and_2_out, and_3_out, and_4_out, and_5_out, and_6_out, and_7_out, and_8_out, and_9_out, and_10_out, and_11_out);
  or or_2 (out_7, and_12_out, and_13_out, and_14_out, and_15_out, and_16_out, and_17_out);
  xnor xnor_1 (out_6, out_5, out_7);

  // Notes on the sheet:
  //   CIRCUITO COMPLETO
  //   FORMA MINIMIZZATA
  //   Le Due soluzioni sono sempre identiche quindi 1 è costante = sono uguali
endmodule

module Ese2Output (
  input  S,
  output \output 
);


  assign \output  = S;
endmodule

module Ese2NextState (
  input  I1,
  input  I0,
  input  S,
  output Snext
);


  assign Snext = I1;
  // also tied to GND on the sheet: {I0, S}
endmodule

module Ese2 (
  input  I1,
  input  I0,
  output out_3
);

  wire clock_1_out, d_ff_1_q, ese2nextstate_1_snext;

  Clock clock_1 (.out(clock_1_out));
  Ese2NextState ese2nextstate_1 (.I1(I1), .I0(I0), .S(d_ff_1_q), .Snext(ese2nextstate_1_snext));
  D_Flip_Flop d_ff_1 (.clk(clock_1_out), .D(ese2nextstate_1_snext), .Q(d_ff_1_q));  // open: Qn, preset, en, reset
  Ese2Output ese2output_1 (.S(d_ff_1_q), .\output (out_3));
endmodule

module Ese3Output (
  input  y2,
  input  y1,
  input  y0,
  output out_4
);

  wire and_1_out, and_2_out;

  and and_1 (and_1_out, y2, y1);
  and and_2 (and_2_out, y1, y0);
  or or_1 (out_4, and_1_out, and_2_out);
endmodule

module Ese3NextState (
  input  w,
  input  y2,
  input  y1,
  input  y0,
  output y2_star,
  output y1_star,
  output y0_star
);

  wire and_1_out, and_2_out, and_3_out, and_4_out, and_5_out, and_6_out, and_7_out, and_8_out;

  and and_1 (and_1_out, y2, y0, w);
  and and_2 (and_2_out, ~y2, y0, ~w);  // AND_Gate
  and and_3 (and_3_out, ~y2, y1, ~w);  // AND_Gate
  and and_4 (and_4_out, y2, y1, w);
  and and_5 (and_5_out, ~y0, ~w);  // AND_Gate
  and and_6 (and_6_out, y1, ~w);  // AND_Gate
  and and_7 (and_7_out, y2, ~w);  // AND_Gate
  and and_8 (and_8_out, y2, ~y1, ~y0);  // AND_Gate
  or or_1 (y1_star, and_1_out, and_2_out, and_3_out, and_4_out);
  or or_2 (y0_star, and_5_out, and_6_out, and_7_out, and_8_out);

  assign y2_star = w;
endmodule

module Ese3 (
  input  w,
  output out_2
);

  wire clock_1_out, d_ff_1_q, d_ff_2_q, d_ff_3_q, ese3nextstate_1_y0_star, ese3nextstate_1_y1_star,
       ese3nextstate_1_y2_star;

  Clock clock_1 (.out(clock_1_out));
  Ese3NextState ese3nextstate_1 (
    .w(w), .y2(d_ff_1_q), .y1(d_ff_2_q), .y0(d_ff_3_q), .y2_star(ese3nextstate_1_y2_star),
    .y1_star(ese3nextstate_1_y1_star), .y0_star(ese3nextstate_1_y0_star));
  D_Flip_Flop d_ff_1 (.clk(clock_1_out), .D(ese3nextstate_1_y2_star), .Q(d_ff_1_q));  // open: Qn, preset, en, reset
  D_Flip_Flop d_ff_2 (.clk(clock_1_out), .D(ese3nextstate_1_y1_star), .Q(d_ff_2_q));  // open: Qn, preset, en, reset
  D_Flip_Flop d_ff_3 (.clk(clock_1_out), .D(ese3nextstate_1_y0_star), .Q(d_ff_3_q));  // open: Qn, preset, en, reset
  Ese3Output ese3output_1 (.y2(d_ff_1_q), .y1(d_ff_2_q), .y0(d_ff_3_q), .out_4(out_2));
endmodule
