// Logisim project Corrado-29407A.circ as structural Verilog: 7 circuits, main circuit Ese1
module Ese1 (
  input  C,
  input  A,
  input  T,
  input  F,
  output out_5,
  output out_6,
  output out_7
);

  wire and_1_out, and_2_out, and_3_out, and_4_out, and_5_out, and_6_out, and_7_out, and_8_out, and_9_out,
       and_10_out, and_11_out, and_12_out, and_13_out, and_14_out, and_15_out, and_16_out, and_17_out;

  and and_1 (and_1_out, A, F);
  and and_2 (and_2_out, A, T);
  and and_3 (and_3_out, C, F);
  and and_4 (and_4_out, C, T);
  and and_5 (and_5_out, T, F);
  and and_6 (and_6_out, C, A);
  and and_7 (and_7_out, ~C, ~A, T, F);  // AND_Gate
  and and_8 (and_8_out, ~C, A, ~T, F);  // AND_Gate
  and and_9 (and_9_out, ~C, A, T, ~F);  // AND_Gate
  and and_10 (and_10_out, ~C, A, T, F);  // AND_Gate
  and and_11 (and_11_out, C, ~A, ~T, F);  // AND_Gate
  and and_12 (and_12_out, C, ~A, T, ~F);  // AND_Gate
  and and_13 (and_13_out, C, ~A, T, F);  // AND_Gate
  and and_14 (and_14_out, C, A, ~T, ~F);  // AND_Gate
  and and_15 (and_15_out, C, A, ~T, F);  // AND_Gate
  and and_16 (and_16_out, C, A, T, ~F);  // AND_Gate
  and and_17 (and_17_out, C, A, T, F);
  or or_1 (out_7, and_1_out, and_2_out, and_3_out, and_4_out, and_5_out, and_6_out);
  or or_2 (out_5, and_7_out, and_8_out, and_9_out, and_10_out, and_11_out, and_12_out, and_13_out, and_14_out, and_15_out, and_16_out, and_17_out);
  xnor xnor_1 (out_6, out_5, out_7);

  // Notes on the sheet:
  //   SOP
  //   Minimizzata
endmodule

module Ese2Output (
  input  S1,
  input  S0,
  output \output 
);

  and and_1 (\output , S1, S0);
endmodule

module Ese2NextState (
  input  X,
  input  S1,
  input  S0,
  output S1next,
  output S0next
);

  wire and_1_out, and_2_out, and_3_out, and_4_out;

  and and_1 (and_1_out, ~X, S0);  // AND_Gate
  and and_2 (and_2_out, S1, S0);
  and and_3 (and_3_out, ~X, S1);  // AND_Gate
  and and_4 (and_4_out, ~X, ~S0);  // AND_Gate
  or or_1 (S1next, and_1_out, and_2_out, and_3_out);
  or or_2 (S0next, and_3_out, and_2_out, and_4_out);
endmodule

module Ese2 (
  input  X,
  output out_2
);

  wire clock_1_out, d_ff_1_q, d_ff_2_q, ese2nextstate_1_s0next, ese2nextstate_1_s1next;

  Clock clock_1 (.out(clock_1_out));
  Ese2NextState ese2nextstate_1 (
    .X(X), .S1(d_ff_1_q), .S0(d_ff_2_q), .S1next(ese2nextstate_1_s1next), .S0next(ese2nextstate_1_s0next));
  D_Flip_Flop d_ff_1 (.clk(clock_1_out), .D(ese2nextstate_1_s1next), .Q(d_ff_1_q));  // open: Qn, preset, en, reset
  D_Flip_Flop d_ff_2 (.clk(clock_1_out), .D(ese2nextstate_1_s0next), .Q(d_ff_2_q));  // open: Qn, preset, en, reset
  Ese2Output ese2output_1 (.S1(d_ff_1_q), .S0(d_ff_2_q), .\output (out_2));
endmodule

module Ese3Output (
  input  q1,
  input  q0,
  output o1,
  output o0
);


  assign o0 = q0;
  assign o1 = q1;
endmodule

module Ese3NextOutput (
  input  I,
  input  q1,
  input  q0,
  output q1_star,
  output q0_star
);

  wire and_1_out, and_2_out, and_3_out, and_4_out;

  and and_1 (and_1_out, ~I, q1);  // AND_Gate
  and and_2 (and_2_out, I, q0);
  and and_3 (and_3_out, ~I, q0);  // AND_Gate
  and and_4 (and_4_out, I, ~q1, ~q0);  // AND_Gate
  or or_1 (q1_star, and_1_out, and_2_out);
  or or_2 (q0_star, and_3_out, and_4_out);
endmodule

module Ese3 (
  input  I,
  output o1,
  output o0
);

  wire clock_1_out, d_ff_1_q, d_ff_2_q, ese3nextoutput_1_q0_star, ese3nextoutput_1_q1_star;

  Clock clock_1 (.out(clock_1_out));
  Ese3NextOutput ese3nextoutput_1 (
    .I(I), .q1(d_ff_1_q), .q0(d_ff_2_q), .q1_star(ese3nextoutput_1_q1_star),
    .q0_star(ese3nextoutput_1_q0_star));
  D_Flip_Flop d_ff_1 (.clk(clock_1_out), .D(ese3nextoutput_1_q1_star), .Q(d_ff_1_q));  // open: Qn, preset, en, reset
  D_Flip_Flop d_ff_2 (.clk(clock_1_out), .D(ese3nextoutput_1_q0_star), .Q(d_ff_2_q));  // open: Qn, preset, en, reset
  Ese3Output ese3output_1 (.q1(d_ff_1_q), .q0(d_ff_2_q), .o1(o1), .o0(o0));
endmodule
