// Logisim project ALU.circ as structural Verilog: 4 circuits, main circuit overflow detector
module overflow_detector (
  input  a,
  input  b,
  input  s,
  output out_4
);

  wire and_1_out, and_2_out;

  and and_1 (and_1_out, ~a, ~b, s);  // AND_Gate
  and and_2 (and_2_out, a, b, ~s);  // AND_Gate
  or or_1 (out_4, and_1_out, and_2_out);
endmodule

module ALU_1_BIT (
  input  [1:0] ALUselect,
  input  invertiB,
  input  rIN,
  input  a,
  input  b,
  input  less,
  output out_7,
  output overflow,
  output rOUT
);

  wire adder_1_out, and_1_out, multiplexer_1_out, not_1_out, or_1_out;

  not not_1 (not_1_out, b);
  Multiplexer multiplexer_1 (.in0(b), .in1(not_1_out), .out(multiplexer_1_out), .sel(invertiB));  // open: en
  and and_1 (and_1_out, a, multiplexer_1_out);
  or or_1 (or_1_out, a, multiplexer_1_out);
  Adder #(.width(1)) adder_1 (.a(a), .b(multiplexer_1_out), .out(adder_1_out), .cin(rIN), .cout(rOUT));
  overflow_detector overflow_detector_1 (.a(a), .b(multiplexer_1_out), .s(adder_1_out), .out_4(overflow));
  Multiplexer #(.select(2)) multiplexer_2 (
    .in0(and_1_out), .in1(or_1_out), .in2(adder_1_out), .in3(less), .out(out_7), .sel(ALUselect));  // open: en
endmodule

module ALU_8_BIT (
  input  invertiB,
  input  [1:0] SEL,
  input  a0,
  input  b0,
  input  a1,
  input  b1,
  input  a2,
  input  b2,
  input  a3,
  input  b3,
  input  a4,
  input  b4,
  input  a5,
  input  b5,
  input  a6,
  input  b6,
  input  a7,
  input  b7,
  output out_19,
  output out_20,
  output out_21,
  output out_22,
  output out_23,
  output out_24,
  output out_25,
  output out_26,
  output overflow
);

  wire alu_1_bit_1_rout, alu_1_bit_2_rout, alu_1_bit_3_rout, alu_1_bit_4_rout, alu_1_bit_5_rout,
       alu_1_bit_6_rout, alu_1_bit_7_rout, alu_1_bit_last_1_less_2;

  ALU_1_BIT alu_1_bit_1 (
    .a(a0), .b(b0), .less(alu_1_bit_last_1_less_2), .out_7(out_19), .invertiB(invertiB), .rIN(invertiB),
    .ALUselect(SEL), .rOUT(alu_1_bit_1_rout));  // open: overflow
  ALU_1_BIT alu_1_bit_2 (
    .a(a1), .b(b1), .out_7(out_20), .invertiB(invertiB), .rIN(alu_1_bit_1_rout), .ALUselect(SEL),
    .rOUT(alu_1_bit_2_rout));  // open: less, overflow
  ALU_1_BIT alu_1_bit_3 (
    .a(a2), .b(b2), .out_7(out_21), .invertiB(invertiB), .rIN(alu_1_bit_2_rout), .ALUselect(SEL),
    .rOUT(alu_1_bit_3_rout));  // open: less, overflow
  ALU_1_BIT alu_1_bit_4 (
    .a(a3), .b(b3), .out_7(out_22), .invertiB(invertiB), .rIN(alu_1_bit_3_rout), .ALUselect(SEL),
    .rOUT(alu_1_bit_4_rout));  // open: less, overflow
  ALU_1_BIT alu_1_bit_5 (
    .a(a4), .b(b4), .out_7(out_23), .invertiB(invertiB), .rIN(alu_1_bit_4_rout), .ALUselect(SEL),
    .rOUT(alu_1_bit_5_rout));  // open: less, overflow
  ALU_1_BIT alu_1_bit_6 (
    .a(a5), .b(b5), .out_7(out_24), .invertiB(invertiB), .rIN(alu_1_bit_5_rout), .ALUselect(SEL),
    .rOUT(alu_1_bit_6_rout));  // open: less, overflow
  ALU_1_BIT alu_1_bit_7 (
    .a(a6), .b(b6), .out_7(out_25), .invertiB(invertiB), .rIN(alu_1_bit_6_rout), .ALUselect(SEL),
    .rOUT(alu_1_bit_7_rout));  // open: less, overflow
  ALU_1_BIT_LAST alu_1_bit_last_1 (
    .a(a7), .b(b7), .out_7(out_26), .less_2(alu_1_bit_last_1_less_2), .overflow(overflow),
    .invertiB(invertiB), .rIN(alu_1_bit_7_rout), .ALUselect(SEL));  // open: less, rOUT
endmodule

module ALU_1_BIT_LAST (
  input  [1:0] ALUselect,
  input  invertiB,
  input  rIN,
  input  a,
  input  b,
  input  less,
  output out_7,
  output less_2,
  output overflow,
  output rOUT
);

  wire and_1_out, multiplexer_1_out, not_1_out, or_1_out;

  not not_1 (not_1_out, b);
  Multiplexer multiplexer_1 (.in0(b), .in1(not_1_out), .out(multiplexer_1_out), .sel(invertiB));  // open: en
  and and_1 (and_1_out, a, multiplexer_1_out);
  or or_1 (or_1_out, a, multiplexer_1_out);
  Adder #(.width(1)) adder_1 (.a(a), .b(multiplexer_1_out), .out(less_2), .cin(rIN), .cout(rOUT));
  overflow_detector overflow_detector_1 (.a(a), .b(multiplexer_1_out), .s(less_2), .out_4(overflow));
  Multiplexer #(.select(2)) multiplexer_2 (
    .in0(and_1_out), .in1(or_1_out), .in2(less_2), .in3(less), .out(out_7), .sel(ALUselect));  // open: en
endmodule
