// Logisim project Ese1.circ as structural Verilog: 4 circuits, main circuit Ese1
module Ese1 (
  input  A,
  input  B,
  input  C,
  output out_4
);

  wire and_1_out, and_2_out, and_3_out, and_4_out, and_5_out, or_1_out, or_2_out;

  and and_1 (and_1_out, A, B);
  and and_2 (and_2_out, A, C);
  and and_3 (and_3_out, B, C);
  and and_4 (and_4_out, A, B, C);
  or or_1 (or_1_out, A, B, C);
  or or_2 (or_2_out, and_1_out, and_2_out, and_3_out);
  and and_5 (and_5_out, or_1_out, ~or_2_out);  // AND_Gate
  or or_3 (out_4, and_4_out, and_5_out);
endmodule

module Es1Controllo (
  input  A,
  input  B,
  input  C,
  output x
);

  wire and_1_out, and_2_out, and_3_out, and_4_out, not_1_out, not_2_out, not_3_out, not_4_out, not_5_out,
       not_6_out;

  not not_1 (not_1_out, A);
  not not_2 (not_2_out, B);
  not not_3 (not_3_out, A);
  not not_4 (not_4_out, C);
  not not_5 (not_5_out, B);
  not not_6 (not_6_out, C);
  and and_1 (and_1_out, not_1_out, not_2_out, C);
  and and_2 (and_2_out, not_3_out, B, not_4_out);
  and and_3 (and_3_out, A, not_5_out, not_6_out);
  and and_4 (and_4_out, A, B, C);
  or or_1 (x, and_1_out, and_2_out, and_3_out, and_4_out);
endmodule

module Ese2 (
  output out_1
);

  wire clock_1_out, d_ff_1_q, d_ff_2_q, ese2next_1_s0_star, ese2next_1_s1_star;

  Clock clock_1 (.out(clock_1_out));
  Ese2Next ese2next_1 (
    .X(d_ff_1_q), .S1(d_ff_2_q), .S0(out_1), .S1_star(ese2next_1_s1_star), .S0_star(ese2next_1_s0_star));
  D_Flip_Flop d_ff_1 (.clk(clock_1_out), .D(ese2next_1_s1_star), .Q(d_ff_1_q));  // open: Qn, preset, en, reset
  D_Flip_Flop d_ff_2 (.clk(clock_1_out), .D(ese2next_1_s0_star), .Q(d_ff_2_q));  // open: Qn, preset, en, reset
endmodule

module Ese2Next (
  input  X,
  input  S1,
  input  S0,
  output S1_star,
  output S0_star
);

  wire and_1_out, and_2_out, and_3_out, and_4_out, not_1_out, not_2_out, not_3_out;

  and and_1 (and_1_out, X, S0);
  and and_2 (and_2_out, X, S1);
  not not_1 (not_1_out, X);
  not not_2 (not_2_out, S1);
  not not_3 (not_3_out, S0);
  or or_1 (S1_star, and_1_out, and_2_out);
  and and_3 (and_3_out, not_1_out, S1);
  and and_4 (and_4_out, X, not_2_out, not_3_out);
  or or_2 (S0_star, and_3_out, and_4_out);
endmodule
