// Logisim project Esercizi.circ as structural Verilog: 3 circuits, main circuit Q* e Q
module Q__e_Q (
  input  [2:0] Q012,
  output [2:0] Q012_star
);

  wire and_1_out;

  not not_1 (Q012_star[0], Q012[0]);
  xor xor_1 (Q012_star[1], Q012[0], Q012[1]);
  and and_1 (and_1_out, Q012[0], Q012[1]);
  xor xor_2 (Q012_star[2], and_1_out, Q012[2]);
endmodule

module Es1 (
);

  wire clock_1_out;
  wire [2:0] d_ff_1_q, q_e_q_1_q012_star;

  Clock clock_1 (.out(clock_1_out));
  D_Flip_Flop d_ff_1 (.clk(clock_1_out), .D(q_e_q_1_q012_star[0]), .Q(d_ff_1_q[0]));  // open: Qn, preset, en, reset
  D_Flip_Flop d_ff_2 (.clk(clock_1_out), .D(q_e_q_1_q012_star[1]), .Q(d_ff_1_q[1]));  // open: Qn, preset, en, reset
  D_Flip_Flop d_ff_3 (.clk(clock_1_out), .D(q_e_q_1_q012_star[2]), .Q(d_ff_1_q[2]));  // open: Qn, preset, en, reset
  Q__e_Q q_e_q_1 (.Q012(d_ff_1_q), .Q012_star(q_e_q_1_q012_star));
  Hex_Digit_Display hex_digit_display_1 (.value({1'b0, d_ff_1_q}));  // open: dp
endmodule

module Es2 (
  input  Seed,
  input  [3:0] Seed_2
);

  wire c, multiplexer_1_out, multiplexer_2_out, multiplexer_3_out, multiplexer_4_out, xor_1_out;
  wire [3:0] d_ff_4_q;

  Clock clock_1 (.out(c));
  D_Flip_Flop d_ff_1 (.clk(c), .D(multiplexer_1_out), .Q(d_ff_4_q[3]));  // open: Qn, preset, en, reset
  Multiplexer multiplexer_1 (.in0(xor_1_out), .in1(Seed_2[0]), .out(multiplexer_1_out), .sel(Seed));  // open: en
  Multiplexer multiplexer_2 (.in0(d_ff_4_q[3]), .in1(Seed_2[1]), .out(multiplexer_2_out), .sel(Seed));  // open: en
  Hex_Digit_Display hex_digit_display_1 (.value(d_ff_4_q));  // open: dp
  D_Flip_Flop d_ff_2 (.clk(c), .D(multiplexer_2_out), .Q(d_ff_4_q[2]));  // open: Qn, preset, en, reset
  xor xor_1 (xor_1_out, d_ff_4_q[0], d_ff_4_q[1]);
  Multiplexer multiplexer_3 (.in0(d_ff_4_q[2]), .in1(Seed_2[2]), .out(multiplexer_3_out), .sel(Seed));  // open: en
  D_Flip_Flop d_ff_3 (.clk(c), .D(multiplexer_3_out), .Q(d_ff_4_q[1]));  // open: Qn, preset, en, reset
  Multiplexer multiplexer_4 (.in0(d_ff_4_q[1]), .in1(Seed_2[3]), .out(multiplexer_4_out), .sel(Seed));  // open: en
  D_Flip_Flop d_ff_4 (.clk(c), .D(multiplexer_4_out), .Q(d_ff_4_q[0]));  // open: Qn, preset, en, reset

  // Other names for the same wires on the sheet: S = Seed; s0 = Seed_2[0]; s1 = Seed_2[1]; s2 = Seed_2[2];
  //   s3 = Seed_2[3]
endmodule
