// Logisim project Esercizi_MSF_Basilico.circ as structural Verilog: 9 circuits, main circuit Esercizio 1 - Output
module Esercizio_1___Output (
  input  X0,
  output \output 
);

  not not_1 (\output , X0);
endmodule

module Esercizio_1___Next_State (
  input  I1,
  input  I0,
  input  X1,
  input  X0,
  output out_5,
  output out_6
);

  wire and_1_out, and_2_out, and_3_out, and_4_out;

  and and_1 (and_1_out, I1, ~I0);  // AND_Gate
  and and_2 (and_2_out, X0, ~I0);  // AND_Gate
  and and_3 (and_3_out, I1, I0);
  and and_4 (and_4_out, X1, ~I1, ~I0);  // AND_Gate
  or or_1 (out_5, and_1_out, and_2_out);
  or or_2 (out_6, and_3_out, and_4_out);
endmodule

module Esercizio_1___MSF (
  input  I1,
  input  I0,
  output out_3
);

  wire clock_1_out, d_ff_1_q, d_ff_2_q, d_ff_2_qn, esercizio_1_next_state_1_out_5,
       esercizio_1_next_state_1_out_6;

  Clock clock_1 (.out(clock_1_out));
  Esercizio_1___Next_State esercizio_1_next_state_1 (
    .I1(I1), .I0(I0), .X1(d_ff_1_q), .X0(d_ff_2_qn), .out_5(esercizio_1_next_state_1_out_5),
    .out_6(esercizio_1_next_state_1_out_6));
  D_Flip_Flop d_ff_1 (
    .clk(clock_1_out), .D(esercizio_1_next_state_1_out_6), .Q(d_ff_1_q));  // open: Qn, preset, en, reset
  D_Flip_Flop d_ff_2 (
    .clk(clock_1_out), .D(esercizio_1_next_state_1_out_5), .Q(d_ff_2_q), .Qn(d_ff_2_qn));  // open: preset, en, reset
  Esercizio_1___Output esercizio_1_output_1 (.X0(d_ff_2_q), .\output (out_3));
endmodule

module Esercizio_2___Output (
  input  X2,
  input  X1,
  input  X0,
  output out_4
);

  and and_1 (out_4, X2, ~X1, X0);  // AND_Gate
endmodule

module Esercizio_2___Next_State (
  input  I,
  input  X2,
  input  X1,
  input  X0,
  output X2_prime,
  output X1_prime,
  output X0_prime
);


  assign X0_prime = X1;
  assign X1_prime = X2;
  assign X2_prime = I;
  // also tied to GND on the sheet: X0
endmodule

module Esercizio_2___MSF (
  input  I,
  output out_2
);

  wire clock_1_out, d_ff_1_q, d_ff_2_q, d_ff_3_q, esercizio_2_next_state_1_x0_prime,
       esercizio_2_next_state_1_x1_prime, esercizio_2_next_state_1_x2_prime;

  Clock clock_1 (.out(clock_1_out));
  Esercizio_2___Next_State esercizio_2_next_state_1 (
    .I(I), .X2(d_ff_1_q), .X1(d_ff_2_q), .X0(d_ff_3_q), .X2_prime(esercizio_2_next_state_1_x2_prime),
    .X1_prime(esercizio_2_next_state_1_x1_prime), .X0_prime(esercizio_2_next_state_1_x0_prime));
  D_Flip_Flop d_ff_1 (
    .clk(clock_1_out), .D(esercizio_2_next_state_1_x2_prime), .Q(d_ff_1_q));  // open: Qn, preset, en, reset
  D_Flip_Flop d_ff_2 (
    .clk(clock_1_out), .D(esercizio_2_next_state_1_x1_prime), .Q(d_ff_2_q));  // open: Qn, preset, en, reset
  D_Flip_Flop d_ff_3 (
    .clk(clock_1_out), .D(esercizio_2_next_state_1_x0_prime), .Q(d_ff_3_q));  // open: Qn, preset, en, reset
  Esercizio_2___Output esercizio_2_output_1 (.X2(d_ff_1_q), .X1(d_ff_2_q), .X0(d_ff_3_q), .out_4(out_2));
endmodule

module Esercizio_3___Output (
  input  X2,
  input  X1,
  input  X0,
  input  in_4,
  input  in_5,
  output Y1,
  output Y0,
  output out_8,
  output out_9
);

  wire and_1_out;

  and and_1 (and_1_out, ~X2, X1, X0);  // AND_Gate
  nor nor_1 (out_8, in_4, out_9);
  nor nor_2 (out_9, out_8, in_5);
endmodule

module Esercizio_3___Next_State (
  input  I,
  input  X2,
  input  X1,
  input  X0,
  output X2_prime,
  output X1_prime,
  output X0_prime
);


  assign X0_prime = X1;
  assign X1_prime = X2;
  assign X2_prime = I;
  // also tied to GND on the sheet: X0
endmodule

module Esercizio_3___MSF (
  input  I
);

  wire clock_1_out, d_ff_1_q, d_ff_2_q, d_ff_3_q, esercizio_3_next_state_1_x0_prime,
       esercizio_3_next_state_1_x1_prime, esercizio_3_next_state_1_x2_prime;

  Clock clock_1 (.out(clock_1_out));
  Esercizio_3___Next_State esercizio_3_next_state_1 (
    .I(I), .X2(d_ff_1_q), .X1(d_ff_2_q), .X0(d_ff_3_q), .X2_prime(esercizio_3_next_state_1_x2_prime),
    .X1_prime(esercizio_3_next_state_1_x1_prime), .X0_prime(esercizio_3_next_state_1_x0_prime));
  D_Flip_Flop d_ff_1 (
    .clk(clock_1_out), .D(esercizio_3_next_state_1_x2_prime), .Q(d_ff_1_q));  // open: Qn, preset, en, reset
  D_Flip_Flop d_ff_2 (
    .clk(clock_1_out), .D(esercizio_3_next_state_1_x1_prime), .Q(d_ff_2_q));  // open: Qn, preset, en, reset
  D_Flip_Flop d_ff_3 (
    .clk(clock_1_out), .D(esercizio_3_next_state_1_x0_prime), .Q(d_ff_3_q));  // open: Qn, preset, en, reset
  Esercizio_3___Output esercizio_3_output_1 (
    .X2(d_ff_1_q), .X1(d_ff_2_q), .X0(d_ff_3_q));  // open: Y1, Y0, in_4, in_5, out_8, out_9
endmodule
