// Logisim project Slide_2.circ as structural Verilog: 5 circuits, main circuit Esercizio 1
module Esercizio_1 (
  input  A,
  input  C,
  input  B,
  output NOT_A,
  output NOT_A_v_C,
  output NOT_A_v_C___A_v_B,
  output A_v_B
);

  not not_1 (NOT_A, A);
  or or_1 (NOT_A_v_C, NOT_A, C);
  or or_2 (A_v_B, A, B);
  and and_1 (NOT_A_v_C___A_v_B, NOT_A_v_C, A_v_B);
endmodule

module Esercizio_2 (
  input  A,
  input  B,
  output XNOR
);

  wire and_1_out, not_1_out, or_1_out;

  or or_1 (or_1_out, A, B);
  and and_1 (and_1_out, A, B);
  not not_1 (not_1_out, or_1_out);
  or or_2 (XNOR, not_1_out, and_1_out);
endmodule

module Esercizio_3 (
  input  A,
  input  B,
  input  C,
  output nA_v_n_B_v_nC
);

  wire not_1_out, not_2_out, not_3_out, or_1_out;

  not not_1 (not_1_out, C);
  not not_2 (not_2_out, A);
  or or_1 (or_1_out, B, not_1_out);
  not not_3 (not_3_out, or_1_out);
  or or_2 (nA_v_n_B_v_nC, not_2_out, not_3_out);
endmodule

module Esercizio_4 (
  input  A,
  input  B,
  input  C,
  output out_4,
  output out_5,
  output out_6
);

  wire and_1_out, and_2_out, and_3_out, and_4_out, not_1_out, not_2_out, not_3_out, not_4_out, or_1_out;

  not not_1 (not_1_out, A);
  not not_2 (not_2_out, C);
  not not_3 (not_3_out, B);
  and and_1 (and_1_out, A, not_3_out);
  and and_2 (and_2_out, A, C);
  and and_3 (and_3_out, not_1_out, B, not_2_out);
  and and_4 (and_4_out, A, B, not_2_out);
  or or_1 (or_1_out, and_3_out, and_4_out);
  or or_2 (out_6, and_1_out, and_2_out);
  not not_4 (not_4_out, or_1_out);
  and and_5 (out_4, not_4_out, A);
  xnor xnor_1 (out_5, out_4, out_6);
endmodule

module Esercizio_5 (
  input  A,
  input  B,
  input  C,
  output out_4
);

  wire nand_1_out, nand_2_out, nand_3_out, nand_4_out, nand_5_out, nand_6_out, nand_7_out;

  nand nand_1 (nand_1_out, A, A);
  nand nand_2 (nand_2_out, B, B);
  nand nand_3 (nand_3_out, C, C);
  nand nand_4 (nand_4_out, nand_1_out, nand_2_out);
  nand nand_5 (nand_5_out, B, nand_3_out);
  nand nand_6 (nand_6_out, nand_4_out, nand_4_out);
  nand nand_7 (nand_7_out, nand_6_out, nand_5_out);
  nand nand_8 (out_4, nand_7_out, nand_7_out);
endmodule
