// Logisim project Slide_3.circ as structural Verilog: 4 circuits, main circuit Esercizio 1
module Esercizio_1 (
  input  A,
  input  B,
  input  in_3,
  input  in_4,
  output out_5,
  output out_6
);

  wire and_1_out, and_2_out, not_1_out, not_2_out, not_3_out, not_4_out, or_1_out, or_2_out;

  not not_1 (not_1_out, A);
  not not_2 (not_2_out, B);
  not not_3 (not_3_out, in_3);
  not not_4 (not_4_out, in_4);
  and and_1 (and_1_out, not_1_out, B);
  and and_2 (and_2_out, not_2_out, A);
  or or_1 (or_1_out, not_3_out, not_4_out);
  or or_2 (or_2_out, in_3, in_4);
  or or_3 (out_5, and_1_out, and_2_out);
  and and_3 (out_6, or_1_out, or_2_out);

  // Notes on the sheet:
  //   SOP
  //   POS
endmodule

module Esercizio_2 (
  input  A,
  input  B,
  input  C,
  input  D,
  input  A_2,
  input  B_2,
  input  C_2,
  input  D_2,
  output out_9,
  output out_10
);

  wire and_1_out, and_2_out, and_3_out, and_4_out, and_5_out, and_6_out, and_7_out, and_8_out, and_9_out,
       and_10_out, and_11_out, not_1_out, or_1_out, or_2_out;

  not not_1 (not_1_out, B);
  or or_1 (or_1_out, A, not_1_out);
  or or_2 (or_2_out, B, C);
  and and_1 (and_1_out, not_1_out, D);
  and and_2 (and_2_out, ~A_2, ~B_2, ~C_2, D_2);  // AND_Gate
  and and_3 (and_3_out, ~A_2, ~B_2, C_2, D_2);  // AND_Gate
  and and_4 (and_4_out, A_2, ~B_2, ~C_2, D_2);  // AND_Gate
  and and_5 (and_5_out, A_2, ~B_2, C_2, ~D_2);  // AND_Gate
  and and_6 (and_6_out, A_2, ~B_2, C_2, D_2);  // AND_Gate
  and and_7 (and_7_out, A_2, B_2, ~C_2, ~D_2);  // AND_Gate
  and and_8 (and_8_out, A_2, B_2, ~C_2, D_2);  // AND_Gate
  and and_9 (and_9_out, A_2, B_2, C_2, ~D_2);  // AND_Gate
  and and_10 (and_10_out, A_2, B_2, C_2, D_2);
  and and_11 (and_11_out, A, or_1_out, or_2_out);
  or or_3 (out_10, and_2_out, and_3_out, and_4_out, and_5_out, and_6_out, and_7_out, and_8_out, and_9_out, and_10_out);
  or or_4 (out_9, and_11_out, and_1_out);

  // Notes on the sheet:
  //   Normale
  //   SOP
endmodule

module Esercizio_3 (
  input  A,
  input  B,
  input  C,
  output Y
);

  wire and_1_out, and_2_out, and_3_out;

  and and_1 (and_1_out, ~A, B);  // AND_Gate
  and and_2 (and_2_out, A, C);
  and and_3 (and_3_out, B, C);
  or or_1 (Y, and_1_out, ~and_2_out, and_3_out);  // OR_Gate
endmodule

module Esercizio_4 (
  input  A,
  input  B,
  input  C,
  output Y
);

  wire and_1_out, and_2_out, or_1_out, or_2_out;

  and and_1 (and_1_out, A, B);
  or or_1 (or_1_out, B, C);
  and and_2 (and_2_out, A, C);
  or or_2 (or_2_out, ~or_1_out, and_2_out);  // OR_Gate
  or or_3 (Y, and_1_out, or_2_out);
endmodule
