// Logisim project Slide_4.circ as structural Verilog: 8 circuits, main circuit Esercizio 1 - Decoder
module Esercizio_1___Decoder (
  input  b1,
  input  b0,
  output _00,
  output _01,
  output _10,
  output _11
);

  and and_1 (_00, ~b1, ~b0);  // AND_Gate
  and and_2 (_01, ~b1, b0);  // AND_Gate
  and and_3 (_10, b1, ~b0);  // AND_Gate
  and and_4 (_11, b1, b0);
endmodule

module Esercizio_1___Multiplexer (
  input  [3:0] in_1,
  input  in_2,
  input  in_3,
  output out_4
);

  wire and_1_out, and_2_out, and_3_out, and_4_out, esercizio_1_decoder_1__00, esercizio_1_decoder_1__01,
       esercizio_1_decoder_1__10, esercizio_1_decoder_1__11;

  Esercizio_1___Decoder esercizio_1_decoder_1 (
    .b1(in_2), .b0(in_3), ._00(esercizio_1_decoder_1__00), ._01(esercizio_1_decoder_1__01),
    ._10(esercizio_1_decoder_1__10), ._11(esercizio_1_decoder_1__11));
  and and_1 (and_1_out, in_1[0], esercizio_1_decoder_1__00);
  and and_2 (and_2_out, in_1[1], esercizio_1_decoder_1__01);
  and and_3 (and_3_out, in_1[2], esercizio_1_decoder_1__10);
  and and_4 (and_4_out, in_1[3], esercizio_1_decoder_1__11);
  or or_1 (out_4, and_1_out, and_2_out, and_3_out, and_4_out);
endmodule

module Esercizio_2___Half_Adder (
  input  b1,
  input  b0,
  output Somma,
  output Riporto
);

  xor xor_1 (Somma, b1, b0);
  and and_1 (Riporto, b0, b1);
endmodule

module Esercizio_3___Full_Adder (
  input  Resto,
  input  b1,
  input  b0,
  input  Resto_2,
  input  b1_2,
  input  b0_2,
  output out_7,
  output out_8
);

  wire and_1_out, and_2_out, and_3_out, esercizio_2_half_adder_1_p3, esercizio_2_half_adder_1_p4, xor_1_out;

  xor xor_1 (xor_1_out, b1, b0);
  and and_1 (and_1_out, b0, b1);
  // Esercizio_2___Half_Adder esercizio_2_half_adder_1: pin names not known; wires that end beside it: b1_2, b0_2, esercizio_2_half_adder_1_p3, esercizio_2_half_adder_1_p4
  and and_2 (and_2_out, Resto_2, esercizio_2_half_adder_1_p3);
  and and_3 (and_3_out, Resto, xor_1_out);
  or or_1 (out_8, and_2_out, esercizio_2_half_adder_1_p4);
  or or_2 (out_7, and_3_out, and_1_out);

  // Notes on the sheet:
  //   SISTEMARE - NON CORRETTO
endmodule

module Esercizio_4___Adder_4_bit (
  input  [3:0] a,
  input  [3:0] b,
  output [3:0] a___b
);

  wire adder_1_cout, adder_2_cout, esercizio_2_half_adder_1_riporto;

  Esercizio_2___Half_Adder esercizio_2_half_adder_1 (
    .b1(a[0]), .b0(b[0]), .Somma(a___b[0]), .Riporto(esercizio_2_half_adder_1_riporto));
  Adder #(.width(1)) adder_1 (
    .a(a[1]), .b(b[1]), .out(a___b[1]), .cin(esercizio_2_half_adder_1_riporto), .cout(adder_1_cout));
  Adder #(.width(1)) adder_2 (.a(a[2]), .b(b[2]), .out(a___b[2]), .cin(adder_1_cout), .cout(adder_2_cout));
  Adder #(.width(1)) adder_3 (.a(a[3]), .b(b[3]), .out(a___b[3]), .cin(adder_2_cout));  // open: cout
endmodule

module Esercizio_5___Complemento_a_2 (
  input  [3:0] in_1,
  output [3:0] out_2,
  output out_3
);

  wire [3:0] not_1_out;

  assign not_1_out = ~in_1;  // NOT_Gate not_1, 4 bits wide
  Adder #(.width(4)) adder_1 (.a(not_1_out), .b(4'b0001), .out(out_2), .cout(out_3));  // open: cin
endmodule

module Esercizio_6___Somma_e_Differenza (
  input  [3:0] B,
  input  [3:0] A,
  input  in_3,
  output [3:0] out_4
);

  wire [3:0] xor_1_out;

  xor xor_1 (xor_1_out[0], in_3, B[0]);
  Adder #(.width(4)) adder_1 (.a(xor_1_out), .b(A), .out(out_4), .cin(in_3));  // open: cout
  xor xor_2 (xor_1_out[1], B[1], in_3);
  xor xor_3 (xor_1_out[2], B[2], in_3);
  xor xor_4 (xor_1_out[3], B[3], in_3);
endmodule

module Esercizio_7___Overflow (
  input  [3:0] B,
  input  [3:0] A,
  input  in_3,
  output [3:0] out_4,
  output overflow
);

  wire xor_5_out, xor_6_out;
  wire [3:0] xor_1_out;

  xor xor_1 (xor_1_out[0], in_3, B[0]);
  Adder #(.width(4)) adder_1 (.a(xor_1_out), .b(A), .out(out_4), .cin(in_3));  // open: cout
  xor xor_2 (xor_1_out[1], B[1], in_3);
  xor xor_3 (xor_1_out[2], B[2], in_3);
  xor xor_4 (xor_1_out[3], B[3], in_3);
  xor xor_5 (xor_5_out, xor_1_out[3], out_4[3]);
  xor xor_6 (xor_6_out, out_4[3], A[3]);
  and and_1 (overflow, xor_5_out, xor_6_out);
endmodule
