// Logisim project Slide_5.circ as structural Verilog: 2 circuits, main circuit Esercizio 1 - Latch SR
module Esercizio_1___Latch_SR (
  input  S,
  input  R,
  output nQ,
  output Q
);

  nor nor_1 (nQ, S, Q);
  nor nor_2 (Q, nQ, R);
endmodule

module Esercizio_2___Latch_con_Clock (
  output out_1,
  output out_2
);

  wire and_1_out, and_2_out, button_1_out, clock_1_out, Reset_out;

  Button Reset (.out(Reset_out));
  Clock clock_1 (.out(clock_1_out));
  Button button_1 (.out(button_1_out));
  and and_1 (and_1_out, Reset_out, clock_1_out);
  and and_2 (and_2_out, clock_1_out, button_1_out);
  Esercizio_1___Latch_SR esercizio_1_latch_sr_1 (.S(and_1_out), .R(and_2_out), .nQ(out_1), .Q(out_2));
endmodule
