// Logisim project Slide_7.circ as structural Verilog: 9 circuits, main circuit Esercizio 1 - Output
module Esercizio_1___Output (
  input  X2,
  input  X1,
  input  X0,
  output \output 
);

  wire and_1_out, and_2_out;

  and and_1 (and_1_out, ~X2, X1, ~X0);  // AND_Gate
  and and_2 (and_2_out, X2, ~X1, X0);  // AND_Gate
  or or_1 (\output , and_1_out, and_2_out);
endmodule

module Esercizio_1___Next_State (
  input  I,
  input  X2,
  input  X1,
  input  X0,
  output X2_prime,
  output X1_prime,
  output X0_prime
);


  assign X0_prime = X1;
  assign X1_prime = X2;
  assign X2_prime = I;
  // also tied to GND on the sheet: X0
endmodule

module Esercizio_1___MSF (
  input  X,
  output out_2
);

  wire clock_1_out, d_ff_1_q, d_ff_2_q, esercizio_1_next_state_1_x0_prime, esercizio_1_next_state_1_x1_prime,
       esercizio_1_next_state_1_x2_prime, t_ff_1_q;

  Clock clock_1 (.out(clock_1_out));
  Esercizio_1___Next_State esercizio_1_next_state_1 (
    .I(X), .X2(d_ff_1_q), .X1(d_ff_2_q), .X0(t_ff_1_q), .X2_prime(esercizio_1_next_state_1_x2_prime),
    .X1_prime(esercizio_1_next_state_1_x1_prime), .X0_prime(esercizio_1_next_state_1_x0_prime));
  D_Flip_Flop d_ff_1 (
    .clk(clock_1_out), .D(esercizio_1_next_state_1_x2_prime), .Q(d_ff_1_q));  // open: Qn, preset, en, reset
  D_Flip_Flop d_ff_2 (
    .clk(clock_1_out), .D(esercizio_1_next_state_1_x1_prime), .Q(d_ff_2_q));  // open: Qn, preset, en, reset
  T_Flip_Flop t_ff_1 (
    .clk(clock_1_out), .T(esercizio_1_next_state_1_x0_prime), .Q(t_ff_1_q));  // open: Qn, preset, reset, en
  Esercizio_1___Output esercizio_1_output_1 (.\output (out_2), .X2(t_ff_1_q), .X1(d_ff_2_q), .X0(d_ff_1_q));
endmodule

module Esercizio_2___Output (
  input  X1,
  output Output
);


  assign Output = X1;
endmodule

module Esercizio_2___Next_State (
  input  I1,
  input  I0,
  input  X1,
  input  X0,
  output X1_prime,
  output X0_prime
);

  wire and_1_out, and_2_out, xor_1_out;

  xor xor_1 (xor_1_out, I1, I0);
  and and_1 (and_1_out, xor_1_out, X0);
  and and_2 (and_2_out, I1, I0);
  xor xor_2 (X1_prime, xor_1_out, X0);
  or or_1 (X0_prime, and_1_out, and_2_out);
  // also tied to GND on the sheet: X1
endmodule

module Esercizio_2___MSF (
  input  I1,
  input  I0,
  output out_3
);

  wire clock_1_out, d_ff_1_q, d_ff_2_q, esercizio_2_next_state_1_x0_prime, esercizio_2_next_state_1_x1_prime;

  Clock clock_1 (.out(clock_1_out));
  Esercizio_2___Next_State esercizio_2_next_state_1 (
    .I1(I1), .I0(I0), .X1(d_ff_1_q), .X0(d_ff_2_q), .X1_prime(esercizio_2_next_state_1_x1_prime),
    .X0_prime(esercizio_2_next_state_1_x0_prime));
  D_Flip_Flop d_ff_1 (
    .clk(clock_1_out), .D(esercizio_2_next_state_1_x1_prime), .Q(d_ff_1_q));  // open: Qn, preset, en, reset
  D_Flip_Flop d_ff_2 (
    .clk(clock_1_out), .D(esercizio_2_next_state_1_x0_prime), .Q(d_ff_2_q));  // open: Qn, preset, en, reset
  Esercizio_2___Output esercizio_2_output_1 (.X1(d_ff_1_q), .Output(out_3));
endmodule

module Esercizio_3___Output (
  input  X,
  output \output 
);


  assign \output  = X;
endmodule

module Esercizio_3___Next_State (
  input  I,
  input  X,
  output X_prime
);

  xor xor_1 (X_prime, I, X);
endmodule

module Esercizio_3___MSF (
  input  I,
  output out_2
);

  wire clock_1_out, d_ff_1_q, esercizio_3_next_state_1_x_prime;

  Clock clock_1 (.out(clock_1_out));
  Esercizio_3___Next_State esercizio_3_next_state_1 (.I(I), .X(d_ff_1_q), .X_prime(esercizio_3_next_state_1_x_prime));
  D_Flip_Flop d_ff_1 (
    .clk(clock_1_out), .D(esercizio_3_next_state_1_x_prime), .Q(d_ff_1_q));  // open: Qn, preset, en, reset
  Esercizio_3___Output esercizio_3_output_1 (.X(d_ff_1_q), .\output (out_2));
endmodule
