// Logisim project EserciziEsameLab.circ as structural Verilog: 6 circuits, main circuit Es1
module Es1 (
  input  A,
  input  B,
  output out_3
);

  wire and_1_out, and_2_out, not_1_out, not_2_out;

  not not_1 (not_1_out, A);
  not not_2 (not_2_out, B);
  and and_1 (and_1_out, A, B);
  and and_2 (and_2_out, not_1_out, not_2_out);
  or or_1 (out_3, and_1_out, and_2_out);
endmodule

module Es2 (
  input  A,
  input  B,
  input  C,
  output out_4
);

  wire not_1_out, not_2_out, not_3_out, or_1_out;

  not not_1 (not_1_out, C);
  not not_2 (not_2_out, A);
  or or_1 (or_1_out, B, not_1_out);
  not not_3 (not_3_out, or_1_out);
  or or_2 (out_4, not_2_out, not_3_out);
endmodule

module Es3 (
  input  A,
  input  B,
  input  C,
  input  D,
  output out_5
);

  wire and_1_out, not_1_out, or_1_out, or_2_out, or_3_out;

  not not_1 (not_1_out, B);
  or or_1 (or_1_out, A, not_1_out);
  or or_2 (or_2_out, B, C);
  or or_3 (or_3_out, not_1_out, D);
  and and_1 (and_1_out, A, or_1_out, or_2_out);
  or or_4 (out_5, and_1_out, or_3_out);
endmodule

module Output_MSF (
  input  S0,
  input  S1,
  input  S2,
  output \output 
);

  wire and_1_out, and_2_out;

  and and_1 (and_1_out, ~S0, S1, ~S2);  // AND_Gate
  and and_2 (and_2_out, S0, ~S1, S2);  // AND_Gate
  or or_1 (\output , and_1_out, and_2_out);
endmodule

module Stato_Prossimo_MSF (
  input  X,
  input  S0,
  input  S1,
  input  S2,
  output S_prime_0,
  output S_prime_1,
  output S_prime_2
);


  assign S_prime_0 = X;
  assign S_prime_1 = S0;
  assign S_prime_2 = S1;
  // also tied to GND on the sheet: S2
endmodule

module MSF (
  input  X,
  output out_2
);

  wire clock_1_out, d_ff_1_q, d_ff_2_q, d_ff_3_q, stato_prossimo_msf_1_s_prime_0,
       stato_prossimo_msf_1_s_prime_1, stato_prossimo_msf_1_s_prime_2;

  Clock clock_1 (.out(clock_1_out));
  Stato_Prossimo_MSF stato_prossimo_msf_1 (
    .X(X), .S0(d_ff_1_q), .S1(d_ff_2_q), .S2(d_ff_3_q), .S_prime_0(stato_prossimo_msf_1_s_prime_0),
    .S_prime_1(stato_prossimo_msf_1_s_prime_1), .S_prime_2(stato_prossimo_msf_1_s_prime_2));
  D_Flip_Flop d_ff_1 (
    .clk(clock_1_out), .D(stato_prossimo_msf_1_s_prime_0), .Q(d_ff_1_q));  // open: Qn, preset, en, reset
  D_Flip_Flop d_ff_2 (
    .clk(clock_1_out), .D(stato_prossimo_msf_1_s_prime_1), .Q(d_ff_2_q));  // open: Qn, preset, en, reset
  D_Flip_Flop d_ff_3 (
    .clk(clock_1_out), .D(stato_prossimo_msf_1_s_prime_2), .Q(d_ff_3_q));  // open: Qn, preset, en, reset
  Output_MSF output_msf_1 (.S0(d_ff_1_q), .S1(d_ff_2_q), .S2(d_ff_3_q), .\output (out_2));
endmodule
