// Logisim project Firmware.circ as structural Verilog: 5 circuits, main circuit main
module main (
  input  [3:0] A,
  input  [3:0] B,
  input  Load,
  input  Start,
  input  Clock,
  output [7:0] A_esteso_e_shiftato,
  output [7:0] P,
  output [7:0] A_b_k,
  output [7:0] B_esteso,
  output [1:0] k
);

  wire Store;
  wire [7:0] alu_1_r;

  Shift8 shift8_1 (.A({4'b0000, A}), .Clock(Store), .Shift(Start), .Load(Load), .R(A_esteso_e_shiftato));
  Shift8 shift8_2 (.A({4'b0000, B}), .Clock(1'b0), .Shift(1'b0), .Load(Load), .R(B_esteso));
  logica logica_1 (.Load(Load), .Start(Start), .Clock(Clock), .k(k), .Store(Store));
  A_b_k a_b_k_1 (.A(A_esteso_e_shiftato), .B(B_esteso), .k(k), .A_b_k(A_b_k));
  ALU alu_1 (.A(P), .B(A_b_k), .R(alu_1_r));
  Shift8 shift8_3 (.A(alu_1_r), .Clock(1'b0), .Shift(1'b0), .Load(Store), .R(P));
  Hex_Digit_Display hex_digit_display_1 (.value(P[7:4]));  // open: dp
  Hex_Digit_Display hex_digit_display_2 (.value(P[3:0]));  // open: dp
endmodule

// RS8
module Shift8 (
  input  [7:0] A,
  input  Clock,
  input  Shift,
  input  Load,
  output [7:0] R
);

  wire and_1_out, multiplexer_1_out, multiplexer_2_out, multiplexer_3_out, multiplexer_4_out,
       multiplexer_5_out, multiplexer_6_out, multiplexer_7_out, multiplexer_8_out, Next;

  and and_1 (and_1_out, Clock, Shift);
  or or_1 (Next, and_1_out, Load);
  Multiplexer multiplexer_1 (.in0(A[0]), .in1(1'b0), .out(multiplexer_1_out), .sel(Shift));  // open: en
  Multiplexer multiplexer_2 (.in0(A[1]), .in1(R[0]), .out(multiplexer_2_out), .sel(Shift));  // open: en
  Multiplexer multiplexer_3 (.in0(A[2]), .in1(R[1]), .out(multiplexer_3_out), .sel(Shift));  // open: en
  Multiplexer multiplexer_4 (.in0(A[3]), .in1(R[2]), .out(multiplexer_4_out), .sel(Shift));  // open: en
  Multiplexer multiplexer_5 (.in0(A[4]), .in1(R[3]), .out(multiplexer_5_out), .sel(Shift));  // open: en
  Multiplexer multiplexer_6 (.in0(A[5]), .in1(R[4]), .out(multiplexer_6_out), .sel(Shift));  // open: en
  Multiplexer multiplexer_7 (.in0(A[6]), .in1(R[5]), .out(multiplexer_7_out), .sel(Shift));  // open: en
  Multiplexer multiplexer_8 (.in0(A[7]), .in1(R[6]), .out(multiplexer_8_out), .sel(Shift));  // open: en
  D_Flip_Flop d_ff_1 (.clk(Next), .D(multiplexer_1_out), .Q(R[0]));  // open: Qn, preset, en, reset
  D_Flip_Flop d_ff_2 (.clk(Next), .D(multiplexer_2_out), .Q(R[1]));  // open: Qn, preset, en, reset
  D_Flip_Flop d_ff_3 (.clk(Next), .D(multiplexer_3_out), .Q(R[2]));  // open: Qn, preset, en, reset
  D_Flip_Flop d_ff_4 (.clk(Next), .D(multiplexer_4_out), .Q(R[3]));  // open: Qn, preset, en, reset
  D_Flip_Flop d_ff_5 (.clk(Next), .D(multiplexer_5_out), .Q(R[4]));  // open: Qn, preset, en, reset
  D_Flip_Flop d_ff_6 (.clk(Next), .D(multiplexer_6_out), .Q(R[5]));  // open: Qn, preset, en, reset
  D_Flip_Flop d_ff_7 (.clk(Next), .D(multiplexer_7_out), .Q(R[6]));  // open: Qn, preset, en, reset
  D_Flip_Flop d_ff_8 (.clk(Next), .D(multiplexer_8_out), .Q(R[7]));  // open: Qn, preset, en, reset

  // Other names for the same wires on the sheet: S = Shift
endmodule

module ALU (
  input  [7:0] A,
  input  [7:0] B,
  output [7:0] R
);

  Adder adder_1 (.a(A), .b(B), .out(R));  // open: cin, cout
endmodule

module A_b_k (
  input  [7:0] A,
  input  [7:0] B,
  input  [1:0] k,
  output [7:0] A_b_k
);

  wire [7:7] multiplexer_1_out;

  Multiplexer #(.select(2)) multiplexer_1 (
    .in0(B[0]), .in1(B[1]), .in2(B[2]), .in3(B[3]), .out(multiplexer_1_out[7]), .sel(k));  // open: en
  assign A_b_k = A & {8{multiplexer_1_out[7]}};  // AND_Gate and_1, 8 bits wide
endmodule

// Logica
module logica (
  input  Load,
  input  Start,
  input  Clock,
  output [1:0] k,
  output Store
);

  nand nand_1 (Store, Start, Clock);
  Counter #(.width(2), .max('h3)) counter_1 (.Q(k), .clk(Store));  // open: load, D, count, carry, clr
  // also tied to GND on the sheet: Load
endmodule
