// Logisim project Lab05.circ as structural Verilog: 8 circuits, main circuit Decodificatore a 2 bit
module Decodificatore_a_2_bit (
  input  b1,
  input  b2,
  output out_3,
  output out_4,
  output out_5,
  output out_6
);

  and and_1 (out_3, ~b1, ~b2);  // AND_Gate
  and and_2 (out_4, ~b1, b2, b2);  // AND_Gate
  and and_3 (out_5, b1, ~b2);  // AND_Gate
  and and_4 (out_6, b1, b2);
endmodule

module Mux_a_4_vie (
  input  [3:0] in_1,
  input  in_2,
  input  in_3,
  output out_4
);

  wire and_1_out, and_2_out, and_3_out, and_4_out, decodificatore_a_2_bit_1_out_3,
       decodificatore_a_2_bit_1_out_4, decodificatore_a_2_bit_1_out_5, decodificatore_a_2_bit_1_out_6;

  Decodificatore_a_2_bit decodificatore_a_2_bit_1 (
    .b1(in_2), .b2(in_3), .out_3(decodificatore_a_2_bit_1_out_3), .out_4(decodificatore_a_2_bit_1_out_4),
    .out_5(decodificatore_a_2_bit_1_out_5), .out_6(decodificatore_a_2_bit_1_out_6));
  and and_1 (and_1_out, in_1[0], decodificatore_a_2_bit_1_out_3);
  and and_2 (and_2_out, in_1[1], decodificatore_a_2_bit_1_out_4);
  and and_3 (and_3_out, in_1[2], decodificatore_a_2_bit_1_out_5, decodificatore_a_2_bit_1_out_5);
  and and_4 (and_4_out, in_1[3], decodificatore_a_2_bit_1_out_6, decodificatore_a_2_bit_1_out_6);
  or or_1 (out_4, and_1_out, and_2_out, and_3_out, and_4_out);
endmodule

module Half_Adder (
  input  A,
  input  B,
  output R,
  output S
);

  xor xor_1 (S, A, B);
  and and_1 (R, A, B);
endmodule

module Full_Adder (
  input  A,
  input  B,
  input  R_IN,
  output R_OUT
);

  wire and_1_out, and_2_out, xor_1_out;

  xor xor_1 (xor_1_out, A, B);
  // XOR_Gate xor_2 has open pins: in1=xor_1_out, in3=R_IN, out=open
  and and_1 (and_1_out, A, B);
  and and_2 (and_2_out, xor_1_out, R_IN);
  xor xor_3 (R_OUT, and_1_out, and_2_out);
endmodule

module Full_Adder__Semplificato (
  input  A,
  input  B,
  input  Rin,
  output Rout,
  output out_5
);

  wire half_adder_2_r, half_adder_r, half_adder_s;

  Half_Adder half_adder (.R(half_adder_r), .A(A), .B(B), .S(half_adder_s));
  Half_Adder half_adder_2 (.R(half_adder_2_r), .A(half_adder_s), .B(Rin), .S(out_5));
  or or_1 (Rout, half_adder_r, half_adder_2_r);
endmodule

module Sommatore_a_4_bit (
  input  [3:0] a,
  input  [3:0] b,
  output [3:0] out_3
);

  wire adder_1_cout, adder_2_cout, half_adder_1_s;

  Half_Adder half_adder_1 (.R(out_3[0]), .A(b[0]), .B(a[0]), .S(half_adder_1_s));
  Adder #(.width(1)) adder_1 (.a(a[1]), .b(b[1]), .out(out_3[1]), .cin(half_adder_1_s), .cout(adder_1_cout));
  Adder #(.width(1)) adder_2 (.a(a[2]), .b(b[2]), .out(out_3[2]), .cin(adder_1_cout), .cout(adder_2_cout));
  Adder #(.width(1)) adder_3 (.a(a[3]), .b(b[3]), .out(out_3[3]), .cin(adder_2_cout));  // open: cout
endmodule

module Complemento_a_2 (
  input  [3:0] in_1,
  output [3:0] out_2,
  output out_3
);

  wire [3:0] not_1_out;

  assign not_1_out = ~in_1;  // NOT_Gate not_1, 4 bits wide
  Adder #(.width(4)) adder_1 (.a(not_1_out), .b(4'b0001), .out(out_2), .cout(out_3));  // open: cin
endmodule

module Somma_o_Differenza (
  input  [3:0] b,
  input  in_2,
  input  [3:0] a,
  output [3:0] out_4,
  output out_5,
  output out_6
);

  wire xor_5_out, xor_6_out;
  wire [3:0] xor_1_out;

  xor xor_1 (xor_1_out[0], b[0], in_2);
  xor xor_2 (xor_1_out[1], b[1], in_2);
  xor xor_3 (xor_1_out[2], b[2], in_2);
  xor xor_4 (xor_1_out[3], b[3], in_2);
  Adder #(.width(4)) adder_1 (.a(xor_1_out), .b(a), .out(out_4), .cout(out_5));  // open: cin
  xor xor_5 (xor_5_out, xor_1_out[3], out_4[3]);
  xor xor_6 (xor_6_out, out_4[3], a[3]);
  and and_1 (out_6, xor_5_out, xor_6_out);
endmodule
