// Logisim project MacchinaDiMoore.circ as structural Verilog: 6 circuits, main circuit Output
module Output (
  input  b2,
  input  b1,
  input  b0,
  output out_4
);

  wire and_1_out, and_2_out;

  and and_1 (and_1_out, ~b0, b1, ~b2);  // AND_Gate
  and and_2 (and_2_out, b0, ~b1, b2);  // AND_Gate
  or or_1 (out_4, and_1_out, and_2_out);
endmodule

module Next (
  input  x,
  input  b0,
  input  b1,
  input  b2,
  output b_prime_0,
  output b_prime_1,
  output b_prime_2
);


  assign b_prime_0 = x;
  assign b_prime_1 = b0;
  assign b_prime_2 = b1;
  // also tied to GND on the sheet: b2
endmodule

module Macchina_Di_Moore (
  input  in_1,
  input  Clock,
  output out_3
);

  wire d_ff_1_q, d_ff_2_q, d_ff_3_q, next_1_b_prime_0, next_1_b_prime_1, next_1_b_prime_2;

  Next next_1 (
    .b_prime_0(next_1_b_prime_0), .b_prime_1(next_1_b_prime_1), .b_prime_2(next_1_b_prime_2), .x(in_1),
    .b0(d_ff_1_q), .b1(d_ff_2_q), .b2(d_ff_3_q));
  D_Flip_Flop d_ff_1 (.clk(Clock), .D(next_1_b_prime_0), .Q(d_ff_1_q));  // open: Qn, preset, en, reset
  D_Flip_Flop d_ff_2 (.clk(Clock), .D(next_1_b_prime_1), .Q(d_ff_2_q));  // open: Qn, preset, en, reset
  D_Flip_Flop d_ff_3 (.clk(Clock), .D(next_1_b_prime_2), .Q(d_ff_3_q));  // open: Qn, preset, en, reset
  Output output_1 (.b2(d_ff_1_q), .b1(d_ff_2_q), .b0(d_ff_3_q), .out_4(out_3));
endmodule

module Output_Somma (
  input  S,
  output \output 
);


  assign \output  = S;
endmodule

module Next_Somma (
  input  R,
  input  S,
  input  B,
  input  A,
  output S_prime,
  output R_prime
);

  wire and_1_out, and_2_out, xor_1_out;

  xor xor_1 (xor_1_out, B, A);
  xor xor_2 (S_prime, R, xor_1_out);
  and and_1 (and_1_out, R, xor_1_out);
  and and_2 (and_2_out, B, A);
  xor xor_3 (R_prime, and_1_out, and_2_out);
  // also tied to GND on the sheet: S
endmodule

module Sommatore_MSF (
  input  A,
  input  B,
  input  in_3,
  output Output
);

  wire d_ff_1_q, d_ff_2_q, next_somma_1_r_prime, next_somma_1_s_prime;

  Next_Somma next_somma_1 (
    .R(A), .S(B), .A(d_ff_2_q), .S_prime(next_somma_1_s_prime), .R_prime(next_somma_1_r_prime));  // open: B
  D_Flip_Flop d_ff_1 (.clk(in_3), .D(next_somma_1_s_prime), .Q(d_ff_1_q));  // open: Qn, preset, en, reset
  D_Flip_Flop d_ff_2 (.clk(in_3), .D(next_somma_1_r_prime), .Q(d_ff_2_q));  // open: Qn, preset, en, reset
  Output_Somma output_somma_1 (.S(d_ff_1_q), .\output (Output));
endmodule
