// Logisim project Memorie.circ as structural Verilog: 11 circuits, main circuit Latch Asincrono SR
module Latch_Asincrono_SR (
  input  in_1,
  input  in_2,
  output out_3,
  output out_4,
  output out_5,
  output out_6
);

  wire button_1_out, button_2_out;

  Clock clock_1 ();  // open: out
  Button button_1 (.out(button_1_out));
  Button button_2 (.out(button_2_out));
  nor Q_star (out_5, button_1_out, out_6);
  nor nor_1 (out_6, out_5, button_2_out);
  nor nor_2 (out_3, in_1, out_4);
  nor nor_3 (out_4, out_3, in_2);

  // Other names for the same wires on the sheet: Q = out_5; Q_star = out_6
endmodule

module Latch_Asincrono_SR_SOP (
  input  in_1,
  input  in_2,
  input  in_3,
  output out_4
);

  wire and_1_out, and_2_out, and_3_out, and_4_out;

  and and_1 (and_1_out, ~in_1, ~in_3);  // AND_Gate
  and and_2 (and_2_out, ~in_1, in_3);  // AND_Gate
  and and_3 (and_3_out, out_4, and_1_out);
  and and_4 (and_4_out, in_2, and_2_out);
  or or_1 (out_4, and_3_out, and_4_out);
endmodule

module Latch_Sincrono_SR (
  input  in_1,
  input  in_2,
  input  in_3,
  output out_4,
  output out_5
);

  wire and_1_out, and_2_out;

  and and_1 (and_1_out, in_1, in_2, in_2);
  and and_2 (and_2_out, in_2, in_3);
  nor nor_1 (out_4, and_1_out, out_5);
  nor nor_2 (out_5, out_4, and_2_out);
endmodule

// Latch D
module Latch_Sincrono_D (
  input  D,
  input  Clock,
  output Q,
  output Q_star
);

  wire not_1_out;

  not not_1 (not_1_out, D);
  Latch_Sincrono_SR latch_sincrono_sr_1 (.in_1(not_1_out), .in_2(Clock), .in_3(D), .out_4(Q), .out_5(Q_star));
endmodule

module Banco_di_memoria_Write (
  input  [3:0] _4_bit_da_memorizzare,
  input  Clock,
  input  Write,
  output [3:0] out_4
);

  wire and_1_out;

  and and_1 (and_1_out, Clock, Write);
  Latch_Sincrono_D latch_sincrono_d_1 (.D(_4_bit_da_memorizzare[0]), .Clock(and_1_out), .Q(out_4[0]));  // open: Q_star
  Latch_Sincrono_D latch_sincrono_d_2 (.D(_4_bit_da_memorizzare[1]), .Clock(and_1_out), .Q(out_4[1]));  // open: Q_star
  Latch_Sincrono_D latch_sincrono_d_3 (.D(_4_bit_da_memorizzare[2]), .Clock(and_1_out), .Q(out_4[2]));  // open: Q_star
  Latch_Sincrono_D latch_sincrono_d_4 (.D(_4_bit_da_memorizzare[3]), .Clock(and_1_out), .Q(out_4[3]));  // open: Q_star
endmodule

module Banco_di_Memoria_Write_Reset (
  input  [3:0] _4_bit_da_memorizzare,
  input  Write,
  input  Reset,
  output [3:0] out_4
);

  wire Clock_out, or_1_out;
  wire [3:0] and_1_out;
  wire [3:3] not_1_out;

  Clock Clock (.out(Clock_out));
  not not_1 (not_1_out[3], Write);
  or or_1 (or_1_out, Write, Reset);
  assign and_1_out = _4_bit_da_memorizzare & {4{not_1_out[3]}};  // AND_Gate and_1, 4 bits wide
  Banco_di_memoria_Write banco_di_memoria_write_1 (
    ._4_bit_da_memorizzare(and_1_out), .Clock(Clock_out), .Write(or_1_out), .out_4(out_4));
endmodule

// FF
module Flip_Flop (
  input  D,
  input  Clock,
  output out_3
);

  wire latch_sincrono_d_1_q, not_1_out;

  Latch_Sincrono_D latch_sincrono_d_1 (.D(D), .Clock(Clock), .Q(latch_sincrono_d_1_q));  // open: Q_star
  Latch_Sincrono_D latch_sincrono_d_2 (.D(latch_sincrono_d_1_q), .Clock(not_1_out), .Q(out_3));  // open: Q_star
  not not_1 (not_1_out, Clock);
endmodule

module Scorrimento (
  input  b_t,
  input  Clock,
  output [3:0] out_3
);

  Flip_Flop flip_flop_1 (.D(b_t), .Clock(Clock), .out_3(out_3[0]));
  Flip_Flop flip_flop_2 (.D(out_3[0]), .Clock(Clock), .out_3(out_3[1]));
  Flip_Flop flip_flop_3 (.D(out_3[1]), .Clock(Clock), .out_3(out_3[2]));
  Flip_Flop flip_flop_4 (.D(out_3[2]), .Clock(Clock), .out_3(out_3[3]));
endmodule

module Banco_di_memoria_con_operazioni (
  input  [3:0] in_1,
  input  Clock,
  input  Reset,
  input  Write,
  input  Shift,
  input  b_t,
  output [3:0] out_7
);

  wire and_2_out, multiplexer_1_out, multiplexer_2_out, multiplexer_3_out, multiplexer_4_out, not_2_out,
       or_1_out;
  wire [3:0] and_1_out;
  wire [3:3] not_1_out;

  not not_1 (not_1_out[3], Reset);
  assign and_1_out = in_1 & {4{not_1_out[3]}};  // AND_Gate and_1, 4 bits wide
  or or_1 (or_1_out, Reset, Write, Shift);
  not not_2 (not_2_out, Shift);
  and and_2 (and_2_out, Clock, or_1_out);
  Multiplexer multiplexer_1 (.in0(b_t), .in1(and_1_out[3]), .out(multiplexer_1_out), .en(not_2_out));  // open: sel
  Flip_Flop flip_flop_1 (.D(multiplexer_1_out), .Clock(and_2_out), .out_3(out_7[3]));
  Multiplexer multiplexer_2 (.in0(out_7[3]), .in1(and_1_out[2]), .out(multiplexer_2_out), .sel(not_2_out));  // open: en
  Flip_Flop flip_flop_2 (.D(multiplexer_2_out), .Clock(and_2_out), .out_3(out_7[2]));
  Multiplexer multiplexer_3 (.in0(out_7[2]), .in1(and_1_out[1]), .out(multiplexer_3_out), .sel(not_2_out));  // open: en
  Flip_Flop flip_flop_3 (.D(multiplexer_3_out), .Clock(and_2_out), .out_3(out_7[1]));
  Multiplexer multiplexer_4 (.in0(out_7[1]), .in1(and_1_out[0]), .out(multiplexer_4_out), .sel(not_2_out));  // open: en
  Flip_Flop flip_flop_4 (.D(multiplexer_4_out), .Clock(and_2_out), .out_3(out_7[0]));
endmodule

module Registro_4_bit (
  input  clock,
  input  [3:0] word,
  output out_3,
  output out_4,
  output out_5,
  output out_6
);

  wire d_ff_2_qn;

  D_Flip_Flop d_ff_1 (.clk(clock), .D(word[0]), .Q(out_3));  // open: Qn, preset, en, reset
  D_Flip_Flop d_ff_2 (.clk(clock), .D(word[1]), .Q(out_4), .Qn(d_ff_2_qn));  // open: preset, en, reset
  D_Flip_Flop d_ff_3 (.clk(clock), .D(word[2]), .Q(out_5));  // open: Qn, preset, en, reset
  D_Flip_Flop d_ff_4 (.clk(clock), .D(word[3]), .Q(out_6));  // open: Qn, preset, en, reset
endmodule

module Memoria_4_Parole (
  input  Clock,
  input  [1:0] Adress,
  input  [3:0] Word,
  output [15:0] out_4
);

  wire and_1_out, and_2_out, and_3_out, and_4_out, decoder_1_out0, decoder_1_out1, decoder_1_out2,
       decoder_1_out3;

  Decoder #(.select(2)) decoder_1 (
    .out0(decoder_1_out0), .out1(decoder_1_out1), .out2(decoder_1_out2), .out3(decoder_1_out3), .sel(Adress));  // open: en
  and and_1 (and_1_out, Clock, decoder_1_out0);
  and and_2 (and_2_out, Clock, decoder_1_out1);
  and and_3 (and_3_out, Clock, decoder_1_out2);
  and and_4 (and_4_out, Clock, decoder_1_out3);
  Registro_4_bit registro_4_bit_1 (
    .clock(and_1_out), .word(Word), .out_3(out_4[0]), .out_4(out_4[1]), .out_5(out_4[2]), .out_6(out_4[3]));
  Registro_4_bit registro_4_bit_2 (
    .clock(and_2_out), .word(Word), .out_3(out_4[4]), .out_4(out_4[5]), .out_5(out_4[6]), .out_6(out_4[7]));
  Registro_4_bit registro_4_bit_3 (
    .clock(and_3_out), .word(Word), .out_3(out_4[8]), .out_4(out_4[9]), .out_5(out_4[10]), .out_6(out_4[11]));
  Registro_4_bit registro_4_bit_4 (
    .clock(and_4_out), .word(Word), .out_3(out_4[12]), .out_4(out_4[13]), .out_5(out_4[14]), .out_6(out_4[15]));
endmodule
